// Logisim project aula-01.circ as structural Verilog: 1 circuit, main circuit main
module main (
  input  A,
  input  B,
  input  A_2,
  input  B_2,
  output Soma,
  output Soma_2,
  output Vai_um
);

  wire and_1_out, and_2_out, and_3_out, and_4_out, not_1_out, not_2_out, not_3_out, not_4_out;

  not not_1 (not_1_out, A_2);
  not not_2 (not_2_out, B);
  not not_3 (not_3_out, A);
  not not_4 (not_4_out, B_2);
  and and_1 (and_1_out, not_2_out, A);
  and and_2 (and_2_out, B, not_3_out);
  and and_3 (and_3_out, not_1_out, B_2);
  and and_4 (and_4_out, A_2, not_4_out);
  and and_5 (Vai_um, A_2, B_2);
  or or_1 (Soma, and_1_out, and_2_out);
  or or_2 (Soma_2, and_3_out, and_4_out);
endmodule
