// Logisim project aula-02.circ as structural Verilog: 1 circuit, main circuit main
module main (
  input  A,
  input  B,
  output AMARELO,
  output D,
  output C
);

  wire and_1_out, and_2_out, and_3_out, and_4_out, not_1_out, not_2_out, or_2_out;

  not not_1 (not_1_out, A);
  not not_2 (not_2_out, B);
  and and_1 (and_1_out, not_1_out, not_2_out);
  and and_2 (and_2_out, A, B);
  and and_3 (and_3_out, not_1_out, B);
  and and_4 (and_4_out, A, not_2_out);
  or or_1 (AMARELO, and_1_out, and_2_out);
  or or_2 (or_2_out, and_3_out, and_4_out);
  and and_5 (D, not_2_out, or_2_out);
  and and_6 (C, or_2_out, not_1_out);
endmodule
