// Logisim project aula-03.circ as structural Verilog: 1 circuit, main circuit main
module main (
  input  Andar_1,
  input  Andar_2,
  input  Andar_3,
  output Desligado,
  output Fraco,
  output \Médio ,
  output Forte
);

  wire and_2_out, and_3_out, and_4_out, and_5_out, and_6_out, and_7_out, not_1_out, not_2_out, not_3_out;

  not not_1 (not_1_out, Andar_1);
  not not_2 (not_2_out, Andar_2);
  not not_3 (not_3_out, Andar_3);
  and and_1 (Desligado, not_1_out, not_2_out, not_3_out);
  and and_2 (and_2_out, Andar_1, not_2_out, not_3_out);
  and and_3 (and_3_out, not_1_out, Andar_2, not_3_out);
  and and_4 (and_4_out, not_1_out, not_2_out, Andar_3);
  and and_5 (and_5_out, Andar_1, Andar_2, not_3_out);
  and and_6 (and_6_out, Andar_1, not_2_out, Andar_3);
  and and_7 (and_7_out, not_1_out, Andar_2, Andar_3);
  and and_8 (Forte, Andar_1, Andar_2, Andar_3);
  or or_1 (Fraco, and_2_out, and_3_out, and_4_out);
  or or_2 (\Médio , and_5_out, and_6_out, and_7_out);
endmodule
