// Logisim project aula-05.circ as structural Verilog: 2 circuits, main circuit somador - 1bit
module somador___1bit (
  input  Vem_um,
  input  A,
  input  B,
  output Soma,
  output Vai_um
);

  wire and_1_out, and_2_out, and_3_out, and_4_out, not_1_out, not_2_out, not_3_out, xor_1_out;

  not not_1 (not_1_out, Vem_um);
  not not_2 (not_2_out, A);
  not not_3 (not_3_out, B);
  and and_1 (and_1_out, not_2_out, B, Vem_um);
  and and_2 (and_2_out, not_3_out, A, Vem_um);
  and and_3 (and_3_out, not_1_out, A, B);
  and and_4 (and_4_out, B, A, Vem_um);
  xor xor_1 (xor_1_out, B, A);
  xor xor_2 (Soma, xor_1_out, Vem_um);
  or or_1 (Vai_um, and_1_out, and_2_out, and_3_out, and_4_out);
endmodule

module somador___2bits (
  input  in_1,
  input  in_2,
  input  in_3,
  input  in_4,
  output out_5,
  output out_6,
  output out_7
);

  wire somador_1bit_1_vai_um;

  somador___1bit somador_1bit_1 (.Vem_um(1'b0), .A(in_3), .B(in_1), .Soma(out_5), .Vai_um(somador_1bit_1_vai_um));
  somador___1bit somador_1bit_2 (.Vem_um(somador_1bit_1_vai_um), .A(in_4), .B(in_2), .Soma(out_6), .Vai_um(out_7));
endmodule
