// Logisim project aula-06.circ as structural Verilog: 2 circuits, main circuit diff 1-bit
module diff_1_bit (
  input  Bin,
  input  A,
  input  B,
  output Diff,
  output Bout
);

  wire and_1_out, and_2_out, and_3_out, and_4_out, not_1_out, not_2_out, not_3_out, xor_1_out;

  not not_1 (not_1_out, Bin);
  not not_2 (not_2_out, A);
  not not_3 (not_3_out, B);
  xor xor_1 (xor_1_out, A, B);
  and and_1 (and_1_out, not_2_out, not_3_out, Bin);
  and and_2 (and_2_out, not_2_out, B, not_1_out);
  and and_3 (and_3_out, not_2_out, B, Bin);
  and and_4 (and_4_out, A, B, Bin);
  xor xor_2 (Diff, xor_1_out, Bin);
  or or_1 (Bout, and_1_out, and_2_out, and_3_out, and_4_out);
endmodule

module diff_2_bit (
  input  A1,
  input  B1,
  input  B2,
  input  A2,
  output out_5,
  output out_6,
  output out_7
);

  wire diff_1_bit_1_bout;

  diff_1_bit diff_1_bit_1 (.Bin(1'b0), .A(A1), .B(B1), .Diff(out_5), .Bout(diff_1_bit_1_bout));
  diff_1_bit diff_1_bit_2 (.Bin(diff_1_bit_1_bout), .A(A2), .B(B2), .Diff(out_6), .Bout(out_7));

  // Notes on the sheet:
  //   Bin
endmodule
