// Logisim project aula-07.circ as structural Verilog: 1 circuit, main circuit main
module main (
  input  C1,
  input  C2,
  input  C3,
  input  A,
  input  B,
  output Resultado
);

  wire and_1_out, and_2_out, and_3_out, and_4_out, and_5_out, and_6_out, not_1_out, not_2_out, not_3_out,
       not_4_out, not_5_out, or_1_out, or_2_out, xor_1_out;

  not not_1 (not_1_out, C1);
  not not_2 (not_2_out, C2);
  not not_3 (not_3_out, C3);
  not not_4 (not_4_out, A);
  not not_5 (not_5_out, B);
  or or_1 (or_1_out, A, B);
  xor xor_1 (xor_1_out, B, A);
  and and_1 (and_1_out, not_2_out, not_3_out, not_1_out);
  and and_2 (and_2_out, C2, not_3_out, not_1_out);
  and and_3 (and_3_out, not_1_out, C3, not_2_out);
  and and_4 (and_4_out, C1, A, not_3_out, B, not_2_out);
  and and_5 (and_5_out, C1, or_1_out, C2, not_3_out);
  or or_2 (or_2_out, and_1_out, and_2_out, and_3_out);
  and and_6 (and_6_out, xor_1_out, or_2_out);
  or or_3 (Resultado, and_4_out, and_5_out, and_6_out);
endmodule
