// Logisim project exercicio-01.circ as structural Verilog: 1 circuit, main circuit main
module main (
  input  A,
  input  B,
  input  C,
  input  D,
  output Soma_01,
  output Soma_02,
  output out_7
);

  wire and_1_out, and_2_out, and_3_out, and_4_out, and_5_out, and_6_out, and_7_out, and_8_out, and_9_out,
       and_10_out, not_1_out, not_2_out, not_3_out, not_4_out, not_5_out, not_6_out, or_2_out;

  not not_1 (not_1_out, A);
  not not_2 (not_2_out, B);
  and and_1 (and_1_out, not_1_out, B);
  and and_2 (and_2_out, A, not_2_out);
  and and_3 (and_3_out, A, B);
  or or_1 (Soma_01, and_1_out, and_2_out);
  not not_3 (not_3_out, C);
  not not_4 (not_4_out, and_3_out);
  not not_5 (not_5_out, D);
  and and_4 (and_4_out, not_3_out, D);
  and and_5 (and_5_out, C, not_5_out);
  and and_6 (and_6_out, C, D);
  and and_7 (and_7_out, not_4_out, and_5_out);
  and and_8 (and_8_out, not_4_out, and_4_out);
  or or_2 (or_2_out, and_4_out, and_5_out);
  not not_6 (not_6_out, or_2_out);
  and and_9 (and_9_out, or_2_out, and_3_out);
  and and_10 (and_10_out, not_6_out, and_3_out);
  or or_3 (out_7, and_9_out, and_6_out);
  or or_4 (Soma_02, and_8_out, and_7_out, and_10_out);

  // Notes on the sheet:
  //   Vem um
endmodule
