// Logisim project somador.circ as structural Verilog: 2 circuits, main circuit somador-1bit
module somador_1bit (
  input  A,
  input  B,
  input  Vem_um,
  output Soma,
  output Vai_um
);

  wire and_1_out, and_2_out, and_3_out, and_4_out, and_5_out, and_6_out, and_7_out, and_8_out, not_1_out,
       not_2_out, not_3_out;

  not not_1 (not_1_out, A);
  not not_2 (not_2_out, B);
  not not_3 (not_3_out, Vem_um);
  and and_1 (and_1_out, not_3_out, B, not_1_out);
  and and_2 (and_2_out, not_3_out, not_2_out, A);
  and and_3 (and_3_out, Vem_um, not_2_out, not_1_out);
  and and_4 (and_4_out, Vem_um, B, A);
  and and_5 (and_5_out, not_3_out, B, A);
  and and_6 (and_6_out, Vem_um, not_2_out, B);
  and and_7 (and_7_out, Vem_um, B, not_1_out);
  and and_8 (and_8_out, Vem_um, B, A);
  or or_1 (Soma, and_1_out, and_2_out, and_3_out, and_4_out);
  or or_2 (Vai_um, and_5_out, and_6_out, and_7_out, and_8_out);
endmodule

module somador_2bits (
  input  B,
  input  A,
  input  D,
  input  C,
  output Soma_bit_1,
  output Soma_bit_2,
  output Vai_um_bit_2
);

  wire somador_1bit_1_vai_um;

  somador_1bit somador_1bit_1 (.A(A), .B(B), .Vem_um(1'b0), .Soma(Soma_bit_1), .Vai_um(somador_1bit_1_vai_um));
  somador_1bit somador_1bit_2 (.A(C), .B(D), .Vem_um(somador_1bit_1_vai_um), .Soma(Soma_bit_2), .Vai_um(Vai_um_bit_2));
endmodule
